// Logisim project __logisim_prontoTeclado.circ as structural Verilog: 2 circuits, main circuit main
module main (
);

  wire _0_out, _1_out, _2_out, _3_out, _4_out, _5_out, _6_out, _7_out, _8_out, _9_out, and_1_out, and_2_out,
       and_3_out, and_4_out, and_5_out, and_6_out, and_7_out, and_8_out, and_9_out, and_10_out, and_11_out,
       and_12_out, and_13_out, and_14_out, and_15_out, and_16_out, decodificador_1_out_11,
       decodificador_1_out_12, decodificador_1_out_13, decodificador_1_out_14, not_1_out, not_2_out,
       not_3_out, not_4_out, or_1_out, or_2_out, or_3_out, or_4_out, or_5_out, or_6_out, or_7_out, XNOR_out;

  Button _1 (.out(_1_out));
  Button _0 (.out(_0_out));
  LED led_1 (.in(decodificador_1_out_11));
  Button _2 (.out(_2_out));
  Button _4 (.out(_4_out));
  Button _3 (.out(_3_out));
  LED led_2 (.in(decodificador_1_out_12));
  not not_1 (not_1_out, decodificador_1_out_12);
  not not_2 (not_2_out, decodificador_1_out_11);
  Button _5 (.out(_5_out));
  Button _6 (.out(_6_out));
  DECODIFICADOR decodificador_1 (
    .in_1(_0_out), .in_2(_1_out), .in_3(_2_out), .in_4(_3_out), .in_5(_4_out), .in_6(_5_out), .in_7(_6_out),
    .in_8(_7_out), .in_9(_8_out), .in_10(_9_out), .out_11(decodificador_1_out_11),
    .out_12(decodificador_1_out_12), .out_13(decodificador_1_out_13), .out_14(decodificador_1_out_14));
  LED led_3 (.in(decodificador_1_out_13));
  LED led_4 (.in(decodificador_1_out_14));
  not not_3 (not_3_out, decodificador_1_out_13);
  Button _9 (.out(_9_out));
  Button _7 (.out(_7_out));
  Button _8 (.out(_8_out));
  not not_4 (not_4_out, decodificador_1_out_14);
  xnor XNOR (XNOR_out, decodificador_1_out_12, decodificador_1_out_14);
  and and_1 (and_1_out, not_3_out, not_4_out);
  and and_2 (and_2_out, decodificador_1_out_13, decodificador_1_out_14);
  and and_3 (and_3_out, decodificador_1_out_12, decodificador_1_out_12, not_3_out, decodificador_1_out_14, decodificador_1_out_14);
  and and_4 (and_4_out, not_2_out, not_1_out, decodificador_1_out_13);
  and and_5 (and_5_out, decodificador_1_out_13, not_4_out);
  and and_6 (and_6_out, not_1_out, not_4_out);
  and and_7 (and_7_out, not_4_out, decodificador_1_out_13);
  and and_8 (and_8_out, decodificador_1_out_11, decodificador_1_out_12);
  and and_9 (and_9_out, decodificador_1_out_11, decodificador_1_out_13);
  and and_10 (and_10_out, not_1_out, not_4_out);
  and and_11 (and_11_out, decodificador_1_out_12, not_4_out);
  and and_12 (and_12_out, decodificador_1_out_12, not_3_out);
  and and_13 (and_13_out, not_3_out, not_4_out);
  and and_14 (and_14_out, decodificador_1_out_12, not_3_out);
  and and_15 (and_15_out, not_1_out, decodificador_1_out_13);
  and and_16 (and_16_out, decodificador_1_out_13, not_4_out);
  or or_1 (or_1_out, XNOR_out, decodificador_1_out_11, decodificador_1_out_13);
  or or_2 (or_2_out, decodificador_1_out_11, not_1_out, and_1_out, and_2_out);
  or or_3 (or_3_out, decodificador_1_out_11, decodificador_1_out_12, not_3_out, decodificador_1_out_14);
  or or_4 (or_4_out, decodificador_1_out_11, and_3_out, and_4_out, and_5_out, and_6_out);
  or or_5 (or_5_out, and_7_out, and_8_out, and_9_out, and_10_out);
  or or_6 (or_6_out, and_11_out, and_12_out, and_13_out, decodificador_1_out_11);
  or or_7 (or_7_out, and_14_out, and_15_out, and_16_out, decodificador_1_out_11);
  _7_Segment_Display u_7_segment_display_1 (
    .g(or_7_out), .f(or_6_out), .a(or_1_out), .b(or_2_out), .e(or_5_out), .d(or_4_out), .c(or_3_out));  // open: dp

  // Notes on the sheet:
  //   A
  //   Decodificador
  //   B
  //   C
  //   D
endmodule

module DECODIFICADOR (
  input  in_1,
  input  in_2,
  input  in_3,
  input  in_4,
  input  in_5,
  input  in_6,
  input  in_7,
  input  in_8,
  input  in_9,
  input  in_10,
  output out_11,
  output out_12,
  output out_13,
  output out_14
);

  wire or_1_out;
  wire [3:0] or_2_out;

  or or_1 (or_1_out, in_1, in_2, in_3, in_4, in_5, in_6, in_7, in_8, in_9, in_10);
  or or_2 (or_2_out[0], in_9, in_10);
  or or_3 (or_2_out[1], in_5, in_6, in_7, in_8);
  or or_4 (or_2_out[2], in_3, in_4, in_8, in_7);
  or or_5 (or_2_out[3], in_2, in_4, in_6, in_8, in_10);
  Register #(.width(4)) register_1 (
    .D(or_2_out), .Q({out_14, out_13, out_12, out_11}), .clk(or_1_out));  // open: en, clr

  // Notes on the sheet:
  //   REGISTRADOR DE MEMÓRIA
endmodule
