// Logisim project logisim_modeloInicial.circ as structural Verilog: 2 circuits, main circuit main
module main (
);

  wire _0_out, _1_out, _2_out, _3_out, _4_out, _5_out, _6_out, _7_out, _8_out, _9_out, decoder_out_11,
       decoder_out_12, decoder_out_13, decoder_out_14, not_1_out, not_2_out, not_3_out, not_4_out;

  Button _0 (.out(_0_out));
  Button _1 (.out(_1_out));
  Button _2 (.out(_2_out));
  Button _3 (.out(_3_out));
  Button _4 (.out(_4_out));
  Button _5 (.out(_5_out));
  Button _6 (.out(_6_out));
  Button _7 (.out(_7_out));
  Button _8 (.out(_8_out));
  Button _9 (.out(_9_out));
  decoder decoder (
    ._9(_9_out), .in_2(_8_out), .in_3(_7_out), .in_4(_6_out), .in_5(_5_out), .in_6(_4_out), .in_7(_3_out),
    .in_8(_2_out), .in_9(_1_out), ._0(_0_out), .out_11(decoder_out_11), .out_12(decoder_out_12),
    .out_13(decoder_out_13), .out_14(decoder_out_14));
  LED A (.in(decoder_out_11));
  LED B (.in(decoder_out_12));
  not not_1 (not_1_out, decoder_out_11);
  LED C (.in(decoder_out_13));
  not not_2 (not_2_out, decoder_out_13);
  not not_3 (not_3_out, decoder_out_12);
  LED D (.in(decoder_out_14));
  not not_4 (not_4_out, decoder_out_14);
endmodule

module decoder (
  input  _9,
  input  in_2,
  input  in_3,
  input  in_4,
  input  in_5,
  input  in_6,
  input  in_7,
  input  in_8,
  input  in_9,
  input  _0,
  output out_11,
  output out_12,
  output out_13,
  output out_14
);

  wire or_1_out;
  wire [3:0] or_2_out;

  or or_1 (or_1_out, _9, in_2, in_3, in_4, in_5, in_6, in_7, in_8, in_9, _0);
  or or_2 (or_2_out[0], in_2, _9);
  or or_3 (or_2_out[1], in_3, in_4, in_5, in_6);
  or or_4 (or_2_out[2], in_3, in_4, in_7, in_8);
  or or_5 (or_2_out[3], _9, in_3, in_5, in_7, in_9);
  Register #(.width(4)) register_1 (
    .D(or_2_out), .Q({out_14, out_13, out_12, out_11}), .clk(or_1_out));  // open: en, clr

  // Notes on the sheet:
  //   REGISTRADOR DE MEMÓRIA
endmodule
